# Fritzing sketch fritzingsketch (saved by Fritzing 0.9.2b)
breadboards: 1

parts:
  part = Arduino Uno (Rev3)
  part_2 = Resistor [tolerance=±20% resistance=220 package=THT]
  part_3 = LED - 5mm [color="Green (570nm)" package="5 mm [THT]"]
  S1 = Pushbutton [package=THT]
  S2 = Pushbutton [package=THT]
  S3 = Pushbutton [package=THT]
  S4 = Pushbutton [package=THT]
  part_4 = Resistor [tolerance=±5% resistance=220 package=THT]
  part_5 = Resistor [tolerance=±5% resistance=220 package=THT]
  part_6 = Resistor [tolerance=±5% resistance=220 package=THT]
  part_7 = Resistor [tolerance=±5% resistance=220 package=THT]
  USB_Connected_to_PC = USB connector [package=THT]  # not connected

nets:
  N1: part.D8, S4.leg1, part_7.Pin_1
  N2: part.D13/SCK, part_2.Pin_0
  N3: part.GND, part_3.cathode, part_4.Pin_0, part_5.Pin_0, part_6.Pin_0, part_7.Pin_0
  N4: part.D3_PWM, S1.leg1, part_4.Pin_1
  N5: part.D4, S2.leg1, part_5.Pin_1
  N6: part.D6_PWM, S3.leg1, part_6.Pin_1
  N7: part.5V, S1.leg0, S2.leg0, S3.leg0, S4.leg0
  N8: part_2.Pin_1, part_3.anode
